# Fritzing sketch Smart dustbin (saved by Fritzing 0.9.3b)
breadboards: 1

parts:
  Part1 = Arduino Nano (Rev3.0) (ICSP)
  LED1 = RGB LED (com. anode, rbg) [package="5 mm [THT]"]
  LED2 = RGB LED (com. anode, rbg) [package="5 mm [THT]"]
  J1 = Basic Servo
  J2 = Basic Servo
  M1 = LJ18A3-H-ZBX [package=THT]
  M2 = LJ18A3-H-ZBX [package=THT]
  M3 = fc-51 [package=THT]
  M4 = fc-51 [package=THT]
  M5 = fc-51 [package=THT]
  VCC1 = Battery

nets:
  GND: Part1.GND, Part1.D10, J1.gnd, J2.gnd, M1.VO_(BLU), M2.VO_(BLU), M3.pin2, M4.pin2, M5.pin1, M5.pin2, VCC1.-
  N1: Part1.D2, LED1.red_cathode
  N2: Part1.D3, LED1.green_cathode
  N3: Part1.D4, LED1.blue_cathode
  N4: Part1.D5, LED2.green_cathode
  N5: Part1.D6, LED2.blue_cathode
  N6: Part1.D7, LED2.red_cathode
  N7: Part1.D8, M3.pin1
  N8: Part1.D9, M4.pin1
  N9: Part1.D11/MOSI, J1.pulse
  N10: Part1.D12/MISO, J2.pulse
  N11: Part1.VIN, VCC1.+
  VCC: Part1.5V, LED1.common_anode, LED2.common_anode, J1.vcc, J2.vcc, M1.VI_(BRN), M2.VI_(BRN), M3.pin3, M4.pin3
  N12: Part1.A1, M2.SIG_(BLK)
  N13: Part1.A0, M1.SIG_(BLK)

custom parts:
  LJ18A3-H-ZBX: LJ18A3-H-ZBX Proximity Sensor module.
  Battery: Your standard 2x 18650 battery pack (7,4 Volts)
