# Fritzing sketch Gamepad (saved by Fritzing 0.9.3b)
breadboards: 1

parts:
  Part1 = Arduino Nano (Rev3.0)
  Part2 = InvenSense MPU6050
  S1 = Pushbutton [package="[THT]"]
  S2 = Pushbutton [package="[THT]"]
  S3 = Pushbutton [package="[THT]"]

nets:
  N1: Part1.RESET, Part2.VCC
  GND: Part1.GND, Part2.GND, S1.Pin_1, S1.Pin_2, S2.Pin_3, S2.Pin_4, S3.Pin_1, S3.Pin_2
  N2: Part1.D5, S2.Pin_1, S2.Pin_2
  N3: Part1.D6, S3.Pin_3, S3.Pin_4
  N4: Part1.D7, S1.Pin_3, S1.Pin_4
  N5: Part1.A5, Part2.SCL
  N6: Part1.A4, Part2.SDA
