# Fritzing sketch Fritzing (saved by Fritzing 0.9.3b)
circuit board: 6.47966cm x 5.83459cm

parts:
  Part1 = Arduino Nano (Rev3.0)
  HC-SR04_Sensor_1 = HC-SR04 Ultrasonic Distance Sensor
  VCC1 = Battery block 9V
  S1 = Round Pushbutton
  J1 = Piezo Speaker

nets:
  N1: Part1.D9, HC-SR04_Sensor_1.TRIG
  N2: Part1.D10, HC-SR04_Sensor_1.ECHO
  N3: Part1.D11/MOSI, J1.pin2
  N4: Part1.VIN, S1.leg0
  GND: Part1.GND, HC-SR04_Sensor_1.GND, VCC1.-, J1.pin1
  5V: Part1.5V, HC-SR04_Sensor_1.VCC
  N5: VCC1.+, S1.leg1
